# Fritzing sketch wro schematic circuit (saved by Fritzing 0.9.3b)

parts:
  Servo_Motor = Basic Servo
  Battery_7_4v = BC9VPC [package=bc9vpc]
  Switch = Round Pushbutton
  PWM1 = Header 3 [package=jst-3-pth]
  PWM2 = Header 3 [package=jst-3-pth]
  JP3 = Header 3 [package=jst-3-pth]  # not connected
  USB_Power = Header 2 [package=jst-2-pth]
  Power = Camdenboss CTB0158-2 [part_number=CTB0158-2 package=THT]
  Camera = Rasberry Pi NIOR Camera [chip_label=IC package="DIP (Dual Inline) [THT]"]  # not connected
  TH_GND_VCC = Header 3 [package=jst-3-pth]
  MOTOR_A_B_C = Header 3 [package=jst-3-pth]
  Battery_-_+ = Header 2 [package=r_sw_th]
  MOTOR_A_B_C_2 = Header 3 [package=jst-3-pth]
  BLDC_MOTOR = Header 3 [package=jst-3-pth]  # not connected
  ESC = Header 3 [package=jst-3-pth]  # not connected
  Raspberry_Pi_5 = Raspberry Pi 5
  USB_C_3_0 = Header 1 [package=1x01_offset]
  USB_A_3_0 = Header 1 [package=1x01_offset]

nets:
  N1: Servo_Motor.gnd, PWM1.1
  N2: Servo_Motor.vcc, PWM1.3
  N3: Servo_Motor.pulse, PWM1.2
  N4: Battery_7_4v.V+, Power.terminal_2, Battery_-_+.1
  N5: Battery_7_4v.V-, Switch.leg1
  N6: Switch.leg0, Power.terminal_1, Battery_-_+.2
  N7: PWM2.1, TH_GND_VCC.1
  N8: USB_Power.1, Raspberry_Pi_5.PWR-1
  N9: USB_Power.2, Raspberry_Pi_5.PWR-2
  N10: MOTOR_A_B_C.1, MOTOR_A_B_C_2.1
  N11: MOTOR_A_B_C.2, MOTOR_A_B_C_2.2
  N12: MOTOR_A_B_C.3, MOTOR_A_B_C_2.3
  N13: USB_C_3_0.1, USB_A_3_0.1

notes:
  Expansion Board
  Buzzer
  RGB1 RGB2
  IMU
  Furitek lizard pro
  2s-4s LiPo
  45A
  180A
  BEC: 6V/3A
  Furitek Micro Komodo
  1212 - 3450KV

custom parts:
  Rasberry Pi NIOR Camera: Camera
  Raspberry Pi 5: The RPi5, a faster version of the awesome Raspberry Pi4B ARM Board with 40 pin gpio.
